# Fritzing sketch nano_esp8266_thingspeak (saved by Fritzing 0.9.2b)
breadboards: 1

parts:
  U1 = ESP8266 WiFi Module [part_number=ESP8266]
  NANO = Arduino Nano (Rev3.0)
  D1 = Rectifier Diode [package="Melf DO-213 AA [SMD]"]
  D2 = Rectifier Diode [package="Melf DO-213 AA [SMD]"]
  R1 = Resistor [tolerance=±5% resistance=1k package=THT]
  R2 = Resistor [tolerance=±5% resistance=2.2k package=THT]
  J1 = screw terminal, 3 pins

nets:
  N1: U1.RXD, R1.Pin_0, R2.Pin_1
  N2: U1.VCC, U1.CH_PD, D2.cathode
  GND: U1.GND, NANO.GND, R2.Pin_0
  N3: U1.TXD, NANO.D2
  N4: NANO.D3, R1.Pin_1
  N5: NANO.5V, D1.anode
  N6: NANO.A2, J1.pin1
  N7: NANO.A1, J1.pin2
  N8: NANO.A0, J1.pin3
  N9: D1.cathode, D2.anode

custom parts:
  ESP8266 WiFi Module: Generic WiFi Module based on the ESP8266 with onboard PCB antenna and UART communications
